// Digital circuit ADDER.dig as structural Verilog
module ADDER (
  input  A_1,
  input  A_2,
  input  A_3,
  input  A_4,
  input  A_5,
  input  A_6,
  input  A_7,
  input  A_0,
  input  B_0,
  input  B_1,
  input  B_2,
  input  B_3,
  input  B_4,
  input  B_5,
  input  B_6,
  input  B_7,
  input  SU,
  input  BUS_0,
  input  BUS_1,
  input  BUS_2,
  input  BUS_3,
  input  BUS_4,
  input  BUS_5,
  input  BUS_6,
  input  BUS_7,
  input  EO
);

  wire A1_pin4, A1_pin7, A1_pin11, A1_pin13, A1_pin16, A2_pin7, A2_pin11, A_OUT_pin2, A_OUT_pin3, A_OUT_pin4,
       A_OUT_pin5, A_OUT_pin6, A_OUT_pin7, A_OUT_pin8, A_OUT_pin9, SU_pin8, SU_pin11;

  _74245 A_OUT (
    .pin1(1'b1), .pin2(A_OUT_pin2), .pin3(A_OUT_pin3), .pin4(A_OUT_pin4), .pin5(A_OUT_pin5),
    .pin6(A_OUT_pin6), .pin7(A_OUT_pin7), .pin8(A_OUT_pin8), .pin9(A_OUT_pin9), .pin10(1'b0), .pin11(BUS_0),
    .pin12(BUS_1), .pin13(BUS_2), .pin14(BUS_3), .pin15(BUS_4), .pin16(BUS_5), .pin17(BUS_6), .pin18(BUS_7),
    .pin19(EO), .pin20(1'b1));
  LED led_1 (.in(A_OUT_pin2));
  LED led_2 (.in(A_OUT_pin3));
  LED led_3 (.in(A_OUT_pin4));
  LED led_4 (.in(A_OUT_pin5));
  LED led_5 (.in(A_OUT_pin6));
  LED led_6 (.in(A_OUT_pin7));
  LED led_7 (.in(A_OUT_pin8));
  LED led_8 (.in(A_OUT_pin9));
  _7483 A1 (
    .pin1(A_7), .pin2(A_OUT_pin3), .pin3(A_6), .pin4(A1_pin4), .pin5(1'b1), .pin6(A_OUT_pin4),
    .pin7(A1_pin7), .pin8(A_5), .pin9(A_OUT_pin5), .pin10(A_4), .pin11(A1_pin11), .pin12(1'b0),
    .pin13(A1_pin13), .pin15(A_OUT_pin2), .pin16(A1_pin16));  // open: pin14
  _7486 u_SU (
    .pin1(B_7), .pin2(SU), .pin3(A1_pin16), .pin4(B_6), .pin5(SU), .pin6(A1_pin4), .pin7(1'b0),
    .pin8(SU_pin8), .pin9(B_2), .pin10(SU), .pin11(SU_pin11), .pin12(B_3), .pin13(SU), .pin14(1'b1));
  _7483 A2 (
    .pin1(A_3), .pin2(A_OUT_pin7), .pin3(A_2), .pin4(SU_pin8), .pin5(1'b1), .pin6(A_OUT_pin8),
    .pin7(A2_pin7), .pin8(A_1), .pin9(A_OUT_pin9), .pin10(A_0), .pin11(A2_pin11), .pin12(1'b0), .pin13(SU),
    .pin14(A1_pin13), .pin15(A_OUT_pin6), .pin16(SU_pin11));
  _7486 SU_2 (
    .pin1(B_5), .pin2(SU), .pin3(A1_pin7), .pin4(B_4), .pin5(SU), .pin6(A1_pin11), .pin7(1'b0),
    .pin8(A2_pin11), .pin9(B_0), .pin10(SU), .pin11(A2_pin7), .pin12(B_1), .pin13(SU), .pin14(1'b1));
endmodule
