// Digital circuit REG.dig as structural Verilog
module REG (
  input  CLK,
  input  CLR,
  input  R_W,
  input  LD,
  input  BI0,
  input  BI1,
  input  BI2,
  input  BI3,
  input  BI4,
  input  BI5,
  input  BI6,
  input  BI7,
  output BO0,
  output BO1,
  output BO2,
  output BO3,
  output BO4,
  output BO5,
  output BO6,
  output BO7
);

  _74245 Bus_I_O (
    .pin1(1'b1), .pin2(BO7), .pin3(BO6), .pin4(BO5), .pin5(BO4), .pin6(BO3), .pin7(BO2), .pin8(BO1),
    .pin9(BO0), .pin10(1'b0), .pin11(BI0), .pin12(BI1), .pin13(BI2), .pin14(BI3), .pin15(BI4), .pin16(BI5),
    .pin17(BI6), .pin18(BI7), .pin19(R_W), .pin20(1'b1));
  LED B7 (.in(BO7));
  LED B6 (.in(BO6));
  _74173 _74173_1 (
    .pin1(1'b0), .pin2(1'b0), .pin3(BO7), .pin4(BO6), .pin5(BO5), .pin6(BO4), .pin7(CLK), .pin8(1'b0),
    .pin9(LD), .pin10(LD), .pin11(BI4), .pin12(BI5), .pin13(BI6), .pin14(BI7), .pin15(CLR), .pin16(1'b1));
  LED B4 (.in(BO4));
  LED B5 (.in(BO5));
  LED B3 (.in(BO3));
  LED B1 (.in(BO1));
  LED B2 (.in(BO2));
  LED B0 (.in(BO0));
  _74173 _74173_2 (
    .pin1(1'b0), .pin2(1'b0), .pin3(BO3), .pin4(BO2), .pin5(BO1), .pin6(BO0), .pin7(CLK), .pin8(1'b0),
    .pin9(LD), .pin10(LD), .pin11(BI0), .pin12(BI1), .pin13(BI2), .pin14(BI3), .pin15(CLR), .pin16(1'b1));

  // Notes on the sheet:
  //   CLR: default 1
  //   R_W: default 1
  //   LD: default 1
endmodule
