// Digital circuit SampleRegAdd.dig as structural Verilog
module SampleRegAdd (
  input  LOAD,
  input  CLR,
  input  clk,
  input  in_4,
  input  in_5,
  input  in_6,
  input  in_7,
  input  in_8,
  input  in_9,
  input  in_10,
  input  in_11,
  input  SUB,
  input  in_13,
  input  in_14,
  input  in_15,
  input  in_16,
  input  in_17,
  input  in_18,
  input  in_19,
  input  in_20
);

  wire undriven, undriven_2, undriven_3, undriven_4, undriven_5, undriven_6, undriven_7, undriven_8,
       undriven_9, undriven_10, undriven_11, undriven_12, undriven_13, undriven_14, undriven_15, undriven_16,
       undriven_17, undriven_18, undriven_19, undriven_20, undriven_21;

  REG reg_1 ();
  REG reg_2 ();
  LED led_1 (.in(undriven_8));
  ADDER adder_1 (
    .A_1(undriven_7), .A_3(undriven_5), .A_5(undriven_4), .A_7(undriven_10), .B_0(undriven_2),
    .B_2(undriven), .B_4(undriven_3), .B_6(undriven_6), .SU(undriven_16), .BUS_1(undriven_18),
    .BUS_3(undriven_19), .BUS_5(undriven_20), .BUS_7(undriven_21));  // open: A_2, A_4, A_6, A_0, B_1, B_3, B_5, B_7, BUS_0, BUS_2, BUS_4, BUS_6, EO
  LED led_2 (.in(undriven_9));
  LED led_3 (.in(undriven_11));
  LED led_4 (.in(undriven_12));
  LED led_5 (.in(undriven_13));
  LED led_6 (.in(undriven_14));
  LED led_7 (.in(undriven_15));
  LED led_8 (.in(undriven_17));
endmodule
